# Fritzing sketch R_Pi_Pico_Tests_01 (saved by Fritzing 0.9.4)
breadboards: 1

parts:
  Mod1 = Raspberry Pi Pico
  R1 = Resistor [tolerance=±5% resistance=220 package="1206 [SMD]"]
  LED1 = LED - 5mm [color="Red (633nm)" package="5 mm [THT]"]
  S1 = Pushbutton [package="[SMD]"]

nets:
  N1: Mod1.pin_3, Mod1.pin_8, Mod1.pin_13, Mod1.pin_18, Mod1.pin_23, Mod1.pin_28, Mod1.pin_33, Mod1.pin_38, R1.Pin_0
  N2: Mod1.pin_19, S1.Pin_1, S1.Pin_2
  N3: Mod1.pin_34, LED1.anode
  N4: Mod1.pin_36, S1.Pin_3, S1.Pin_4
  N5: R1.Pin_1, LED1.cathode

custom parts:
  Raspberry Pi Pico: Raspberry Pi Pico. Based around the RP2040 microcontroller the Pico is a low cost microcontroller device bringing Raspberry Pi quality, cost, and easy of use to the microcontroller space. Jan 2021, Split part in to two versions: tht (this one) and SMD. This one will drill holes for a .1 in header in pcb to allow plugging in the module as well as providing pads to solder the module to the top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
