# Fritzing sketch oled_img_002 (saved by Fritzing 0.9.4)
breadboards: 1

parts:
  RP_p1 = Raspberry Pi Pico
  S1 = Pushbutton [package="[THT]"]
  OLED_I2C1 = OLED 128x64 I2C Monochrome Display

nets:
  N1: RP_p1.pin_1, OLED_I2C1.SDA
  N2: RP_p1.pin_2, OLED_I2C1.SCK
  N3: RP_p1.pin_3, RP_p1.pin_28, OLED_I2C1.GND
  N4: RP_p1.pin_19, S1.Pin_1, S1.Pin_2
  N5: RP_p1.pin_36, S1.Pin_3, S1.Pin_4, OLED_I2C1.VDD

custom parts:
  Raspberry Pi Pico: Raspberry Pi Pico. Based around the RP2040 microcontroller the Pico is a low cost microcontroller device bringing Raspberry Pi quality, cost, and easy of use to the microcontroller space. Jan 2021, Split part in to two versions: tht (this one) and SMD. This one will drill holes for a .1 in header in pcb to allow plugging in the module as well as providing pads to solder the module to the top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
